# Fritzing sketch Tracker (saved by Fritzing 0.8.5b)
circuit board: 8.46667cm x 5.64444cm
breadboards: 1

parts:
  Part2 = Arduino GSM Shield
  Part3 = Breadboard Power Supply Board SMD
  LED1 = smd LED [color="Red (633nm)" package="0603 [SMD]"]
  R1 = Resistor [tolerance=±5% resistance=220 package=THT]
  U1 = microSD minibox [package=usd-socket-pp]
  U3 = ET312 GPS Receiver [package=et312]
  Part4 = Arduino Uno (Rev3)  # not connected

nets:
  N1: Part2.SCK/D13, U1.SCK
  N2: Part2.MISO/D12, Part2.SS/PWM_D10, U1.MISO
  N3: Part2.MOSI/PWM_D11, U1.MOSI
  N4: Part2.PWM_D4, U3.RX
  N5: Part2.PWM_D5, U3.TX
  GND: Part3.GND, U1.GND, U3.GND2, U3.GND3, U3.GND4, U3.GND5, U3.GND6, U3.GND7
  VCC: Part3.VCC, LED1.cathode, R1.Pin_1, U1.VCC, U3.VCC
  N6: LED1.anode, R1.Pin_0

custom parts:
  microSD minibox: microSD Socket Push-push type uSD socket. Schematic element and footprint production proven. Spark Fun Electronics SKU : PRT-00127. tDoc lines correctly indicate media card edge positions when inserting (unlocked, locked, depressed).
